# Fritzing sketch leafchamber (saved by Fritzing 0.9.3b)
breadboards: 1

parts:
  Part1 = Arduino Uno (Rev3)
  S1 = Pushbutton [package="[SMD]"]
  S2 = Pushbutton [package="[SMD]"]
  S3 = Pushbutton [package="[SMD]"]
  Part2 = Adafruit TSL2561 [part_number="Adafruit #439"]
  R1 = Resistor [tolerance=±5% resistance=220 package="0805 [SMD]"]
  R2 = Resistor [tolerance=±5% resistance=220 package="0805 [SMD]"]
  R3 = Resistor [tolerance=±5% resistance=220 package="0805 [SMD]"]
  J1 = Basic Servo
  J2 = Basic Servo
  microSD_Transflash2 = SparkFun - microSD Transflash
  CONN1 = USB connector [package=THT]

nets:
  N1: Part1.A0, S1.Pin_1, S1.Pin_2, R1.Pin_0
  N2: Part1.A1, S2.Pin_1, S2.Pin_2, R2.Pin_0
  N3: Part1.A2, S3.Pin_1, S3.Pin_2, R3.Pin_0
  N4: Part1.D8, microSD_Transflash2.CS
  N5: Part1.D9_PWM, J2.pulse
  N6: Part1.D10_PWM/SS, J1.pulse
  N7: Part1.D11_PWM/MOSI, microSD_Transflash2.DO
  N8: Part1.D12/MISO, microSD_Transflash2.DI
  N9: Part1.D13/SCK, microSD_Transflash2.SCK
  N10: Part1.A4/SDA, Part2.SDA
  N11: Part1.A5/SCL, Part2.SCL
  3V3: Part1.3V3, microSD_Transflash2.VCC
  5V: Part1.5V, S1.Pin_3, S1.Pin_4, S2.Pin_3, S2.Pin_4, S3.Pin_3, S3.Pin_4, Part2.VIN, J1.vcc, J2.vcc, CONN1.5V
  GND: Part1.GND, Part2.GND, R1.Pin_1, R2.Pin_1, R3.Pin_1, J1.gnd, J2.gnd, microSD_Transflash2.GND, CONN1.GND, CONN1.chassis5, CONN1.chassis6

custom parts:
  Adafruit TSL2561: The TSL2561 luminosity sensor is an advanced digital light sensor, ideal for use in a wide range of light situations. Compared to low cost CdS cells, this sensor is more precise, allowing for exact lux calculations and can be configured for different gain/timing ranges to detect light ranges from up to 0.1 - 40,000+ Lux on the fly. The best part of this sensor is that it contains both infrared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
  SparkFun - microSD Transflash: https://www.sparkfun.com/products/544 Breakout board for the microSD socket that is not much bigger than your fingernail. Compatible with the SPI interface found on any SD card, this tiny form factor was created for cell phone storage and is perfect for your next MP3 project! Board comes fully assembled and tested. The bare socket is available.
